# Fritzing sketch binary-clock (saved by Fritzing 0.9.4)
breadboards: 1

parts:
  Part1 = Arduino Uno (Rev3)
  R1 = Resistor [tolerance=±1% resistance=100 package=THT]
  R2 = Resistor [tolerance=±1% resistance=100 package=THT]
  R3 = Resistor [tolerance=±1% resistance=100 package=THT]
  R4 = Resistor [tolerance=±1% resistance=100 package=THT]
  R5 = Resistor [tolerance=±1% resistance=100 package=THT]
  R6 = Resistor [tolerance=±1% resistance=100 package=THT]
  R7 = Resistor [tolerance=±1% resistance=100 package=THT]
  R8 = Resistor [tolerance=±1% resistance=100 package=THT]
  R9 = Resistor [tolerance=±1% resistance=100 package=THT]
  R10 = Resistor [tolerance=±1% resistance=100 package=THT]
  R11 = Resistor [tolerance=±1% resistance=100 package=THT]
  LED1 = smd LED [color="White (4500K)" package="1206 [SMD]"]
  LED2 = smd LED [color="White (4500K)" package="1206 [SMD]"]
  LED3 = smd LED [color="White (4500K)" package="1206 [SMD]"]
  LED4 = smd LED [color="White (4500K)" package="1206 [SMD]"]
  LED5 = smd LED [color="White (4500K)" package="1206 [SMD]"]
  LED6 = smd LED [color="White (4500K)" package="1206 [SMD]"]
  LED7 = smd LED [color="White (4500K)" package="1206 [SMD]"]
  LED8 = smd LED [color="White (4500K)" package="1206 [SMD]"]
  LED9 = smd LED [color="White (4500K)" package="1206 [SMD]"]
  LED10 = smd LED [color="White (4500K)" package="1206 [SMD]"]
  LED11 = smd LED [color="White (4500K)" package="1206 [SMD]"]
  S1 = Momentary Switch [package=ksa_sealed_tac_switch]
  R12 = Resistor [tolerance=±5% resistance=10k package="2512 [SMD]"]

nets:
  N1: Part1.D8, LED9.anode
  N2: Part1.D9_PWM, LED10.anode
  N3: Part1.D10_PWM/SS, LED11.anode
  N4: Part1.D11_PWM/MOSI, S1.1
  N5: Part1.D0/RX, LED1.anode
  N6: Part1.D1/TX, LED2.anode
  N7: Part1.D2, LED3.anode
  N8: Part1.D3_PWM, LED4.anode
  N9: Part1.D4, LED5.anode
  N10: Part1.D5_PWM, LED6.anode
  N11: Part1.D6_PWM, LED7.anode
  N12: Part1.D7, LED8.anode
  N13: Part1.5V, S1.3
  N14: R1.Pin_0, LED1.cathode
  GND: R1.Pin_1, R2.Pin_1, R3.Pin_1, R4.Pin_1, R5.Pin_1, R6.Pin_1, R7.Pin_1, R8.Pin_1, R9.Pin_1, R10.Pin_1, R11.Pin_1, R12.Pin_0
  N15: R2.Pin_0, LED2.cathode
  N16: R3.Pin_0, LED3.cathode
  N17: R4.Pin_0, LED4.cathode
  N18: R5.Pin_0, LED5.cathode
  N19: R6.Pin_0, LED6.cathode
  N20: R7.Pin_0, LED8.cathode
  N21: R8.Pin_0, LED7.cathode
  N22: R9.Pin_0, LED9.cathode
  N23: R10.Pin_0, LED10.cathode
  N24: R11.Pin_0, LED11.cathode
  N25: S1.2, R12.Pin_1
